# Fritzing sketch relevador (saved by Fritzing 0.9.3b)
breadboards: 1

parts:
  Componente1 = Arduino Uno (Rev3)
  Q1 = NPN-Transistor [package="SOT-23 [SMD]"]
  D1 = Schottky Diode [part_number=1N5817 package="300 mil [THT]"]
  R1 = Resistor [tolerance=±5% resistance=220 package="0603 [SMD]"]
  K1 = Relay [part_number=FRS1B-S package=THT]
  LED1 = LED - 5mm [color="Red (633nm)" package="5 mm [THT]"]
  PIR1 = PIR sensor

nets:
  N1: Componente1.D3_PWM, PIR1.SIG
  N2: Componente1.D4, R1.Pin_0
  5V: Componente1.5V, Q1.1, D1.cathode, D1.anode, K1.COIL1, K1.COIL2, PIR1.VDD
  GND: Componente1.GND, Q1.2, PIR1.GND
  N3: Q1.0, R1.Pin_1
  N4: K1.C1, K1.C2, LED1.cathode
